# Fritzing sketch KTNE2 (saved by Fritzing 0.9.3b)
breadboards: 1

parts:
  Part1 = Arduino Mega 2560 (Rev3)
  S1 = Pushbutton [package="[SMD]"]
  S2 = Pushbutton [package="[SMD]"]
  S3 = Pushbutton [package="[SMD]"]
  S4 = Pushbutton [package="[SMD]"]
  R1 = Resistor [tolerance=±5% resistance=220 package="2010 [SMD]"]
  R2 = Resistor [tolerance=±5% resistance=220 package="2010 [SMD]"]
  R3 = Resistor [tolerance=±5% resistance=220 package="2010 [SMD]"]
  R4 = Resistor [tolerance=±5% resistance=220 package="2010 [SMD]"]
  R5 = Resistor [tolerance=±5% resistance=220 package="2010 [SMD]"]
  R6 = Resistor [tolerance=±5% resistance=220 package="2010 [SMD]"]
  R8 = Resistor [tolerance=±5% resistance=220 package="2010 [SMD]"]
  D1 = LTE-302 [package=lte-302]
  R9 = Resistor [tolerance=±5% resistance=220 package="2010 [SMD]"]
  D2 = LTE-302 [package=lte-302]
  D3 = LTE-302 [package=lte-302]
  D4 = LTE-302 [package=lte-302]

nets:
  N1: Part1.5V, Part1.D36, S2.Pin_3, S2.Pin_4, S3.Pin_3, S3.Pin_4, S4.Pin_1, S4.Pin_2, R2.Pin_0
  N2: Part1.D30, S1.Pin_1, S1.Pin_2, R4.Pin_1
  N3: Part1.D31, R5.Pin_0
  N4: Part1.D32, S2.Pin_1, S2.Pin_2
  N5: Part1.D33, Part1.D35, D1.A, D2.A, D3.A, D4.A
  N6: Part1.D34, S3.Pin_1, S3.Pin_2, R1.Pin_0
  N7: Part1.D37, R8.Pin_0
  N8: Part1.GND, R3.Pin_0
  N9: S1.Pin_3, S1.Pin_4, R1.Pin_1
  N10: S4.Pin_3, S4.Pin_4
  N11: R2.Pin_1, R4.Pin_0
  N12: R5.Pin_1, R6.Pin_1, R8.Pin_1, R9.Pin_1
